# Fritzing sketch light_test_schematic (saved by Fritzing 0.9.4)

parts:
  Part4 = Arduino Uno (Rev3)
  LED1 = RGB LED (com. cathode, rgb) [package="5 mm [THT]"]

nets:
  N1: Part4.A0, LED1.blue_anode
  N2: Part4.D7, LED1.green_anode
  N3: Part4.5V, LED1.red_anode
  N4: Part4.GND, LED1.common_cathode

notes:
  Using this LED to represent the board.
  From left to right - VCC, GND, D0, A0
