# Fritzing sketch pump_relay_test_schematic (saved by Fritzing 0.9.4)

parts:
  Part3 = Arduino Uno (Rev3)
  WeMos_D1_Mini_Relay_Shield_V1 = WeMos D1 Mini Relay Shield V2
  M1 = DC Motor
  VCC1 = Battery block 9V

nets:
  N1: Part3.D10_PWM/SS, WeMos_D1_Mini_Relay_Shield_V1.D1
  5V: Part3.5V, WeMos_D1_Mini_Relay_Shield_V1.5V
  N2: Part3.GND, WeMos_D1_Mini_Relay_Shield_V1.G
  N3: WeMos_D1_Mini_Relay_Shield_V1.COM, VCC1.+
  N4: WeMos_D1_Mini_Relay_Shield_V1.NO, M1.pin_1

notes:
  NOT THE SAME EXACT RELAY.
  Here - treat D1-D4 as the input pins.
  Actual relay is a 4 channel setup, with 4 input pins, vcc and ground.
  NC = Normally Closed
  NO = Normally Open
  Using DC motor to represent water pump.
  Power supply should be 12V, ~200-300mA
