# Fritzing sketch soil_moisture_test_schematic (saved by Fritzing 0.9.4)
breadboards: 1

parts:
  Part2 = Arduino Uno (Rev3)
  Part3 = Soil Moisture Sensor

nets:
  N1: Part2.A0, Part3.SIG

notes:
  *Not same exact sensor, close enough.
