# Fritzing sketch water_level_test_schematic (saved by Fritzing 0.9.4)

parts:
  Part4 = Arduino Uno (Rev3)
  LED1 = DUO LED RG [package="5 mm [THT]"]

nets:
  N1: Part4.D7, LED1.common_cathode
  N2: Part4.5V, LED1.red_anode
  N3: Part4.GND, LED1.green_anode

notes:
  Using this LED to represent the sensor.
  From left to right, VCC, Data and GND.
