# Fritzing sketch single_arduino_schematic (saved by Fritzing 0.9.4)
breadboards: 1

parts:
  Raspberry_Pi_1 = Raspberry Pi 3 [part_number=RPI-3-V1.2]  # not connected
  U1 = TCM8240MD [package=tcm8240md]  # not connected
  Part1 = Arduino Uno (Rev3) - ICSP
  Part2 = Adafruit Si7021 Temp Humidity [part_number="Adafruit #3251"]

nets:
  N1: Part1.A4/SDA, Part2.SDA
  N2: Part1.A5/SCL, Part2.SCL
  5V: Part1.5V, Part2.VIN
  GND: Part1.GND, Part2.GND

notes:
  Raspberry Pi 3 Model B V1.2
  Arduino Uno
  Raspberry Pi Camera Rev 1.3
  Adafruit Si7021
  Temp. and humidity sensor

custom parts:
  Adafruit Si7021 Temp Humidity: It's summer and you're sweating and your hair's all frizzy and all you really want to know is why the weatherman said this morning that today's relative humidity would max out at a perfectly reasonable 42% when it feels more like 77%. Enter the Si7021 Temperature + Humidity Sensor - the best way to prove the weatherman wrong! This lovely sensor for Silicon labs has ± 3% relative humidity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
